# Fritzing sketch plotter (saved by Fritzing 0.9.3b)
perfboards: 1

parts:
  IC1 = L293D [package=THT]
  IC2 = L293D [package=THT]
  J1 = Basic Servo
  부품1 = Arduino Uno (Rev3)
  M1 = Stepper Motor - Bipolar
  M2 = Stepper Motor - Bipolar
  Grove1 = Grove OLED 128x96

nets:
  VCC: IC1.Enable_1, IC1.+Vmotor, IC1.Enable_2, IC1.+V, IC2.Enable_1, IC2.+Vmotor, IC2.Enable_2, IC2.+V, J1.vcc, 부품1.VIN
  N1: IC1.In_1, 부품1.D2
  N2: IC1.Out_1_(_Controlled_by_Enable_1_), M1.A
  GND: IC1.0V, IC2.0V, J1.gnd, 부품1.GND, Grove1.GND
  N3: IC1.Out_2_(_Controlled_by_Enable_1_), M1.D
  N4: IC1.In_2, 부품1.D3_PWM
  N5: IC1.In_3, 부품1.D4
  N6: IC1.Out_3_(_Controlled_by_Enable_2_), M1.B
  N7: IC1.Out_4_(_Controlled_by_Enable_2_), M1.C
  N8: IC1.In_4, 부품1.D5_PWM
  N9: IC2.In_1, 부품1.D8
  N10: IC2.Out_1_(_Controlled_by_Enable_1_), M2.A
  N11: IC2.Out_2_(_Controlled_by_Enable_1_), M2.D
  N12: IC2.In_2, 부품1.D9_PWM
  N13: IC2.In_3, 부품1.D10_PWM/SS
  N14: IC2.Out_3_(_Controlled_by_Enable_2_), M2.B
  N15: IC2.Out_4_(_Controlled_by_Enable_2_), M2.C
  N16: IC2.In_4, 부품1.D11_PWM/MOSI
  N17: J1.pulse, 부품1.D6_PWM
  N18: 부품1.A4/SDA, Grove1.SDA
  N19: 부품1.A5/SCL, Grove1.SCL
  5V: 부품1.5V, Grove1.VCC

notes:
  X axis
  Y axis
  + 5V POWER -
